// Logisim project Lab 1 Circuit.circ as structural Verilog: 1 circuit, main circuit main
module main (
);

  wire t_ff_1_q;
  wire [2:0] Current_State_q, rom_1_data;
  wire [5:3] rom_1_data_2;

  T_Flip_Flop t_ff_1 (.Q(t_ff_1_q));  // open: clk, T, Qn, preset, reset, en
  Register #(.width(3), .trigger("falling")) Current_State (
    .D(rom_1_data), .Q(Current_State_q), .clk(t_ff_1_q));  // open: en, clr
  LED led_1 (.in(t_ff_1_q));
  ROM #(.addrWidth(3), .dataWidth(6)) rom_1 (.addr(Current_State_q), .data({rom_1_data_2, rom_1_data}));  // open: sel
  LED O2 (.in(rom_1_data_2[5]));
  LED O1 (.in(rom_1_data_2[4]));
  LED O0 (.in(rom_1_data_2[3]));

  // Notes on the sheet:
  //   contents of rom_1 (hex, n*v repeats v):
  //   23 1c 0 35 a 3f 6 39
endmodule
