// Logisim project Lab2 Circuit.circ as structural Verilog: 1 circuit, main circuit main
module main (
  input  in_1
);

  wire Carry_out, comparator_1_lt, comparator_2_lt, N, V, V_t, xnor_1_out, xor_1_out, Z;
  wire [3:0] OP;
  wire [31:0] ADD, NOP, R, SMIN, SMIN_t, UMIN, UMIN_t, X, Y;

  Register #(.width(32)) Input_X (.Q(X));  // open: D, en, clk, clr
  Register #(.width(32)) Input_Y (.Q(Y));  // open: D, en, clk, clr
  Register #(.width(4)) Operational_Selector (.Q(OP));  // open: D, en, clk, clr
  // Probe on R
  LED led_1 (.in(V_t));
  LED led_2 (.in(N));
  LED led_3 (.in(Z));
  LED led_4 (.in(Carry_out));
  Adder #(.width(32)) adder_1 (.a(X), .b(Y), .out(ADD), .cin(in_1), .cout(Carry_out));
  Comparator #(.width(32)) comparator_1 (.a(X), .b(Y), .lt(comparator_1_lt));  // open: gt, eq
  Comparator #(.width(32)) comparator_2 (.a(X), .b(Y), .lt(comparator_2_lt));  // open: gt, eq
  Comparator #(.width(32)) comparator_3 (.a({32{1'b0}}), .b(R), .eq(Z));  // open: gt, lt
  Comparator #(.width(32)) comparator_4 (.a({32{1'b0}}), .b(R), .gt(N));  // open: eq, lt
  Multiplexer #(.width(32)) multiplexer_1 (.in0(Y), .in1(X), .out(SMIN_t), .sel(comparator_1_lt));  // open: en
  Multiplexer #(.width(32)) multiplexer_2 (.in0(Y), .in1(X), .out(UMIN_t), .sel(comparator_2_lt));  // open: en
  xnor xnor_1 (xnor_1_out, X[31], Y[31]);
  Multiplexer #(.select(4), .width(32)) multiplexer_3 (
    .in0(NOP), .in1(ADD), .in2(Y), .in9(UMIN), .in10(SMIN), .out(R), .sel(OP));  // open: in3, in4, in5, in6, in7, in8, in11, in12, in13, in14, in15, en
  xor xor_1 (xor_1_out, Y[31], R[31]);
  and and_1 (V, xnor_1_out, xor_1_out);
endmodule
