// Logisim project Lab-3_Part1 Circuit.circ as structural Verilog: 1 circuit, main circuit main
module main (
);

  wire alu_1_p4, alu_1_p5, alu_1_p6, alu_1_p7, alu_1_p8, CLK, CLR, not_1_out, or_1_out, reg32_1_p5, T1CE,
       T1OE, T2CE, T2OE, WordR, WordW;
  wire [1:0] register_1_q;
  wire [3:0] OPR, Reg;
  wire [31:0] Data, rom_1_data;

  // Probe on rom_1_data[1:0]
  // Probe on register_1_q
  Register #(.width(2)) register_1 (.D(rom_1_data[1:0]), .Q(register_1_q), .clk(CLK), .clr(CLR));  // open: en
  // Reg32 reg32_1: pin names not known; wires that end beside it: Data, CLK, T1CE, T1OE, reg32_1_p5, CLR
  // Probe on {rom_1_data[31:16], OPR, Reg, WordR, WordW, T1CE, T1OE, T2CE, T2OE, rom_1_data[1:0]}
  ROM #(.addrWidth(2), .dataWidth(32)) rom_1 (
    .addr(register_1_q),
    .data({rom_1_data[31:16], OPR, Reg, WordR, WordW, T1CE, T1OE, T2CE, T2OE, rom_1_data[1:0]}));  // open: sel
  // ALU alu_1: pin names not known; wires that end beside it: reg32_1_p5, Data, OPR, alu_1_p4, alu_1_p5, alu_1_p6, alu_1_p7, alu_1_p8
  LED led_1 (.in(alu_1_p5));
  LED led_2 (.in(alu_1_p6));
  LED led_3 (.in(alu_1_p7));
  LED led_4 (.in(alu_1_p8));
  // Reg32 reg32_2: pin names not known; wires that end beside it: alu_1_p4, CLK, T2CE, T2OE, Data, CLR
  // Probe on OPR
  // Probe on Reg
  // Probe on WordR
  // Probe on WordW
  // Probe on T1CE
  // Probe on T1OE
  // Probe on T2CE
  // Probe on T2OE
  Button button_1 (.out(CLR));
  T_Flip_Flop Toggle_Switch (.Q(CLK));  // open: clk, T, Qn, preset, reset, en
  or or_1 (or_1_out, WordW, WordR);
  not not_1 (not_1_out, CLK);
  RAM #(.addrWidth(4), .dataWidth(32)) ram_1 (
    .addr(Reg), .data(Data), .sel(or_1_out), .clk(not_1_out), .ld(WordR), .clr(CLR));

  // Notes on the sheet:
  //   contents of rom_1 (hex, n*v repeats v):
  //   a1 1c9a d44
endmodule
