// Logisim project Lab-3_Part2 Circuit.circ as structural Verilog: 1 circuit, main circuit main
module main (
);

  wire alu_1_p4, alu_1_p5, alu_1_p6, alu_1_p7, alu_1_p8, and_1_out, ANOP, AOP, CLK, CLR, DR, not_1_out,
       or_1_out, reg32_1_p5, src, SXR, SYR, T1CE, T1OE, T2CE, T2OE, WordR, WordW;
  wire [1:0] multiplexer_1_out, register_1_q, rom_1_data;
  wire [3:0] OPR, Reg;
  wire [15:0] IR_q;
  wire [31:0] DATA;

  // Probe on 2'b10
  // Probe on rom_1_data
  Multiplexer #(.width(2), .enable("false")) multiplexer_1 (
    .in0(rom_1_data), .in1(2'b10), .out(multiplexer_1_out), .sel(and_1_out));
  // Reg32 reg32_1: pin names not known; wires that end beside it: CLK, DATA, T1CE, T1OE, reg32_1_p5
  and and_1 (and_1_out, ~register_1_q[0], ~register_1_q[1], src);  // AND_Gate
  or or_1 (or_1_out, WordW, WordR);
  // Probe on register_1_q
  Register #(.width(2)) register_1 (.D(multiplexer_1_out), .Q(register_1_q), .clk(CLK));  // open: en, clr
  not not_1 (not_1_out, CLK);
  // ALU alu_1: pin names not known; wires that end beside it: reg32_1_p5, DATA, OPR, alu_1_p4, alu_1_p5, alu_1_p6, alu_1_p7, alu_1_p8
  RAM #(.addrWidth(4), .dataWidth(32)) ram_1 (
    .addr(Reg), .data(DATA), .sel(or_1_out), .clk(not_1_out), .ld(WordR), .clr(CLR));
  // Probe on DATA
  ROM #(.addrWidth(2), .dataWidth(13)) rom_1 (
    .addr(register_1_q), .data({AOP, ANOP, DR, SXR, SYR, WordR, WordW, T1CE, T1OE, T2CE, T2OE, rom_1_data}));  // open: sel
  LED led_1 (.in(alu_1_p5));
  LED led_2 (.in(alu_1_p6));
  LED led_3 (.in(alu_1_p7));
  LED led_4 (.in(alu_1_p8));
  Register #(.width(16)) IR (.Q(IR_q));  // open: D, en, clk, clr
  // Probe on {AOP, ANOP, DR, SXR, SYR, WordR, WordW, T1CE, T1OE, T2CE, T2OE, rom_1_data}
  // Reg32 reg32_2: pin names not known; wires that end beside it: CLK, alu_1_p4, T2CE, T2OE, DATA
  assign Reg = SYR ? IR_q[3:0] : 4'bz;  // Controlled_Buffer controlled_buffer_1
  assign Reg = SXR ? IR_q[7:4] : 4'bz;  // Controlled_Buffer controlled_buffer_2
  assign Reg = DR ? IR_q[11:8] : 4'bz;  // Controlled_Buffer controlled_buffer_3
  assign OPR = AOP ? IR_q[15:12] : 4'bz;  // Controlled_Buffer controlled_buffer_4
  assign OPR = ANOP ? 4'b0000 : 4'bz;  // Controlled_Buffer controlled_buffer_5
  and and_2 (src, IR_q[12], IR_q[13], ~IR_q[15]);  // AND_Gate
  // Probe on T2OE
  // Probe on T2CE
  // Probe on T1OE
  // Probe on T1CE
  // Probe on WordW
  // Probe on WordR
  // Probe on SYR
  // Probe on SXR
  // Probe on DR
  // Probe on ANOP
  // Probe on AOP
  // Probe on Reg
  // Probe on OPR
  Button button_1 (.out(CLR));
  T_Flip_Flop Toggle_Switch (.Q(CLK));  // open: clk, T, Qn, preset, reset, en

  // Notes on the sheet:
  //   contents of rom_1 (hex, n*v repeats v):
  //   801 aa2 119b c44
endmodule
