// Logisim project Debugger Support.circ as structural Verilog: 3 circuits, main circuit ALU
module ALU (
  input  [31:0] X,
  input  [31:0] Y,
  input  Clock,
  input  Clr_In,
  input  F,
  input  [3:0] Opr,
  output Z,
  output [31:0] R,
  output S,
  output C,
  output V
);

  wire ADD, ADD_or_SUB, adder_1_cout, AND, and_2_out, and_3_out, and_4_out, and_5_out, and_6_out, and_9_out,
       and_10_out, and_11_out, ASL, ASR, DIV, LSL, LSL_Carry, LSR, LSR_Carry, MUL, MULDIVCarry,
       multiplexer_2_out, multiplexer_3_out, NOP, NotY, OR, or_3_out, or_4_out, or_7_out, or_8_out, or_9_out,
       ROL, ROR, RY, SUB, undriven, xnor_1_out, XOR, xor_2_out, xor_3_out, xor_4_out;
  wire [15:0] DIVHigh16, divider_1_rem, REMHigh16;
  wire [31:0] adder_1_out, and_1_out, divider_1_out, multiplexer_1_out, multiplexer_4_out, multiplexer_5_out,
       multiplier_1_cout, multiplier_1_out, not_1_out, or_2_out, shifter_1_out, shifter_2_out, xor_1_out;

  Decoder #(.select(4)) decoder_1 (
    .out0(NOP), .out1(ADD), .out2(SUB), .out3(RY), .out4(AND), .out5(OR), .out6(XOR), .out7(NotY),
    .out8(LSR), .out9(LSL), .out10(ASR), .out11(ASL), .out12(ROR), .out13(ROL), .out14(MUL), .out15(DIV),
    .sel(Opr));  // open: en
  assign xor_1_out = X ^ Y;  // XOR_Gate xor_1, 32 bits wide
  assign not_1_out = ~Y;  // NOT_Gate not_1, 32 bits wide
  assign R = NotY ? not_1_out : 32'bz;  // Controlled_Buffer controlled_buffer_1
  assign R = RY ? Y : 32'bz;  // Controlled_Buffer controlled_buffer_2
  or or_1 (ADD_or_SUB, ADD, SUB);
  assign R = XOR ? xor_1_out : 32'bz;  // Controlled_Buffer controlled_buffer_3
  Multiplexer #(.width(32)) multiplexer_1 (.in0(Y), .in1(not_1_out), .out(multiplexer_1_out), .sel(SUB));  // open: en
  Adder #(.width(32)) adder_1 (.a(X), .b(multiplexer_1_out), .out(adder_1_out), .cin(SUB), .cout(adder_1_cout));
  xor xor_2 (xor_2_out, R[31], X[31]);
  xnor xnor_1 (xnor_1_out, X[31], Y[31]);
  xor xor_3 (xor_3_out, R[31], X[31]);
  xor xor_4 (xor_4_out, X[31], Y[31]);
  assign or_2_out = X | Y;  // OR_Gate or_2, 32 bits wide
  assign and_1_out = X & Y;  // AND_Gate and_1, 32 bits wide
  assign R = AND ? and_1_out : 32'bz;  // Controlled_Buffer controlled_buffer_4
  assign R = ADD_or_SUB ? adder_1_out : 32'bz;  // Controlled_Buffer controlled_buffer_5
  and and_2 (and_2_out, xor_2_out, xnor_1_out, ADD);
  and and_3 (and_3_out, xor_3_out, xor_4_out, SUB);
  Shifter #(.width(32)) shifter_1 (.in(X), .\dist (Y[4:0]), .out(shifter_1_out));
  assign R = OR ? or_2_out : 32'bz;  // Controlled_Buffer controlled_buffer_6
  Shifter #(.width(32), .shift("lr")) shifter_2 (.in(X), .\dist (Y[4:0]), .out(shifter_2_out));
  Multiplexer #(.select(5)) multiplexer_2 (
    .in0(1'b0), .in1(X[0]), .in2(X[1]), .in3(X[2]), .in4(X[3]), .in5(X[4]), .in6(X[5]), .in7(X[6]),
    .in8(X[7]), .in9(X[8]), .in10(X[9]), .in11(X[10]), .in12(X[11]), .in13(X[12]), .in14(X[13]),
    .in15(X[14]), .in16(X[15]), .in17(X[16]), .in18(X[17]), .in19(X[18]), .in20(X[19]), .in21(X[20]),
    .in22(X[21]), .in23(X[22]), .in24(X[23]), .in25(X[24]), .in26(X[25]), .in27(X[26]), .in28(X[27]),
    .in29(X[28]), .in30(X[29]), .in31(X[30]), .out(multiplexer_2_out), .sel(Y[4:0]));  // open: en
  and and_4 (and_4_out, X[31], Y[5]);
  Multiplexer #(.select(5)) multiplexer_3 (
    .in0(X[1]), .in1(X[2]), .in2(X[3]), .in3(X[4]), .in4(X[5]), .in5(X[6]), .in6(X[7]), .in7(X[8]),
    .in8(X[9]), .in9(X[10]), .in10(X[11]), .in11(X[12]), .in12(X[13]), .in13(X[14]), .in14(X[15]),
    .in15(X[16]), .in16(X[17]), .in17(X[18]), .in18(X[19]), .in19(X[20]), .in20(X[21]), .in21(X[22]),
    .in22(X[23]), .in23(X[24]), .in24(X[25]), .in25(X[26]), .in26(X[27]), .in27(X[28]), .in28(X[29]),
    .in29(X[30]), .in30(X[31]), .in31(1'b0), .out(multiplexer_3_out), .sel(Y[4:0]));  // open: en
  and and_5 (and_5_out, adder_1_cout, ADD_or_SUB);
  and and_6 (and_6_out, Y[5], X[0]);
  or or_3 (or_3_out, multiplexer_2_out, and_4_out);
  Multiplexer #(.width(32)) multiplexer_4 (
    .in0(shifter_1_out), .in1({32{1'b0}}), .out(multiplexer_4_out), .sel(Y[5]));  // open: en
  or or_4 (or_4_out, and_6_out, multiplexer_3_out);
  or or_5 (V, and_2_out, and_3_out);
  assign R = LSR ? multiplexer_5_out : 32'bz;  // Controlled_Buffer controlled_buffer_7
  Multiplexer #(.width(32)) multiplexer_5 (
    .in0(shifter_2_out), .in1({32{1'b0}}), .out(multiplexer_5_out), .sel(Y[5]));  // open: en
  and and_7 (LSR_Carry, or_3_out, LSR);
  assign R = LSL ? multiplexer_4_out : 32'bz;  // Controlled_Buffer controlled_buffer_8
  and and_8 (LSL_Carry, or_4_out, LSL);
  or or_6 (C, and_5_out, LSR_Carry, LSL_Carry, MULDIVCarry);
  // Probe on X
  // Probe on Y
  // Probe on multiplier_1_out
  Multiplier #(.width(32)) multiplier_1 (.a(X), .b(Y), .out(multiplier_1_out), .cout(multiplier_1_cout));  // open: cin
  Divider #(.width(32)) divider_1 (.a(X), .b(Y), .out(divider_1_out), .rem({REMHigh16, divider_1_rem}));  // open: upper
  // Probe on {REMHigh16, divider_1_rem}
  nor nor_1 (Z, R[0], R[1], R[2], R[3], R[4], R[5], R[6], R[7], R[8], R[9], R[10], R[11], R[12], R[13], R[14], R[15], R[16], R[17], R[18], R[19], R[20], R[21], R[22], R[23], R[24], R[25], R[26], R[27], R[28], R[29], R[30], R[31]);
  // Probe on undriven
  assign R = MUL ? multiplier_1_out : 32'bz;  // Controlled_Buffer controlled_buffer_9
  assign {DIVHigh16, R[15:0]} = DIV ? divider_1_out : 32'bz;  // Controlled_Buffer controlled_buffer_10
  or or_7 (or_7_out, multiplier_1_cout[0], multiplier_1_cout[1], multiplier_1_cout[2], multiplier_1_cout[3], multiplier_1_cout[4], multiplier_1_cout[5], multiplier_1_cout[6], multiplier_1_cout[7], multiplier_1_cout[8], multiplier_1_cout[9], multiplier_1_cout[10], multiplier_1_cout[11], multiplier_1_cout[12], multiplier_1_cout[13], multiplier_1_cout[14], multiplier_1_cout[15], multiplier_1_cout[16], multiplier_1_cout[17], multiplier_1_cout[18], multiplier_1_cout[19], multiplier_1_cout[20], multiplier_1_cout[21], multiplier_1_cout[22], multiplier_1_cout[23], multiplier_1_cout[24], multiplier_1_cout[25], multiplier_1_cout[26], multiplier_1_cout[27], multiplier_1_cout[28], multiplier_1_cout[29], multiplier_1_cout[30], multiplier_1_cout[31]);
  or or_8 (or_8_out, REMHigh16[0], REMHigh16[1], REMHigh16[2], REMHigh16[3], REMHigh16[4], REMHigh16[5], REMHigh16[6], REMHigh16[7], REMHigh16[8], REMHigh16[9], REMHigh16[10], REMHigh16[11], REMHigh16[12], REMHigh16[13], REMHigh16[14], REMHigh16[15]);
  assign R[31:16] = DIV ? divider_1_rem : 16'bz;  // Controlled_Buffer controlled_buffer_11
  and and_9 (and_9_out, or_7_out, MUL);
  and and_10 (and_10_out, or_8_out, DIV);
  or or_9 (or_9_out, DIVHigh16[0], DIVHigh16[1], DIVHigh16[2], DIVHigh16[3], DIVHigh16[4], DIVHigh16[5], DIVHigh16[6], DIVHigh16[7], DIVHigh16[8], DIVHigh16[9], DIVHigh16[10], DIVHigh16[11], DIVHigh16[12], DIVHigh16[13], DIVHigh16[14], DIVHigh16[15]);
  and and_11 (and_11_out, or_9_out, DIV);
  or or_10 (MULDIVCarry, and_9_out, and_10_out, and_11_out);

  assign S = R[31];

  // Other names for the same wires on the sheet: Clr = Clr_In; msb_R = R[31]; msb_X = X[31]; LSLcount5[4:0] = Y[4:0];
  //   LSRcount5[4:0] = Y[4:0]; LSLcount6 = Y[5]; LSRcount6 = Y[5]; msb_Y = Y[31]

  // Notes on the sheet:
  //   Logical Shift Right = 1000
  //   Logical Shift Right = 1001
  //   Debugger Support Verison 4-2
  //   4-2 FLAGS "out" to PSR rather than latched
  //   4.1  added MUL and DIV and LSL
  //   4.1  added placeholders for additional logical operations
  //   NOP = 0000
  //   ADD = 0001
  //   SUB = 0010
  //   RY = 0011
  //   AND = 0100
  //   OR = 0101
  //   XOR = 0110
  //   NotY = 0111
  //   MUL = 1110
  //   DIV = 1111
  //   Operation Decoder
  //   NOT Y
  //   oVerflow detector
  //   X
  //   Y
  //   Only C = 1  if ADD or SUB
  //   Only V = 1 this way  if ADD
  //   Only V = 1 this way  if SUB
  //   F removed V4-2
  //   Clock removed in V4-2
  //   if F==0 do not update FLAGS
  //   zero detector
  //   FLAG latches removed V 4-2
endmodule

module Reg8 (
  input  [7:0] DIn,
  input  CE,
  input  CLK,
  input  OE,
  output [7:0] Debug_Q,
  output [7:0] DOut
);

  Register #(.trigger("falling")) Logisim_Register (.D(DIn), .en(CE), .Q(Debug_Q), .clk(CLK));  // open: clr
  assign DOut = OE ? Debug_Q : 8'bz;  // Controlled_Buffer controlled_buffer_1
endmodule

module Reg32 (
  input  [31:0] DIn,
  input  CE,
  input  CLK,
  input  OE,
  input  Clear,
  output [31:0] Debug_Q,
  output [31:0] DOut
);

  Register #(.width(32), .trigger("falling")) Logisim_Register (.D(DIn), .en(CE), .Q(Debug_Q), .clk(CLK), .clr(Clear));
  assign DOut = OE ? Debug_Q : 32'bz;  // Controlled_Buffer controlled_buffer_1
endmodule
