// Logisim project Debugger V4-5.circ as structural Verilog: 5 circuits, main circuit Computer System View
module Computer_System_View (
);

  wire button_1_out, button_2_out, button_3_out, button_4_out, button_5_out, Clk, Clr,
       debug_control_panel_1_break_enabled, debug_control_panel_1_c, debug_control_panel_1_i,
       debug_control_panel_1_n, debug_control_panel_1_running, debug_control_panel_1_tick_sensor,
       debug_control_panel_1_v, debug_control_panel_1_z, i_o_1_troll, i_o_1_trunning, LED,
       processor_1_debug_reg_write, Read, SW, Write;
  wire [3:0] H0, H1, processor_1_debug_reg_addrs;
  wire [4:0] processor_1_flags_out;
  wire [6:0] State;
  wire [7:0] INTs;
  wire [31:0] Addrs, debug_control_panel_1_instruction_counter, debug_control_panel_1_r0_data,
       debug_control_panel_1_r1_data, debug_control_panel_1_r2_data, debug_control_panel_1_r3_data,
       debug_control_panel_1_r4_data, debug_control_panel_1_r5_data, debug_control_panel_1_r6_data,
       debug_control_panel_1_r7_data, debug_control_panel_1_r8_data, debug_control_panel_1_r9_data,
       debug_control_panel_1_r10_data, debug_control_panel_1_r11_data, debug_control_panel_1_r12_data,
       debug_control_panel_1_r13_data, debug_control_panel_1_r14_data, debug_control_panel_1_r15_data,
       I_Addrs, i_o_1_tcount, i_o_1_treload, IR, main_memory_1_data_bus_out, processor_1_debug_data_out,
       processor_1_processor_data_bus_out, register_1_q;

  LED led_1 (.in(debug_control_panel_1_running));
  Processor processor_1 (
    .Address_Bus(Addrs), .Processor_Data_Bus_Out(processor_1_processor_data_bus_out),
    .Processor_Data_In(main_memory_1_data_bus_out), .CLK(Clk), .MWrite(Write), .MRead(Read), .Clr(Clr),
    .IReg(IR), .CurrState(State), .Debug_Reg_Write(processor_1_debug_reg_write),
    .Debug_Reg_Addrs(processor_1_debug_reg_addrs), .Debug_Data_out(processor_1_debug_data_out),
    .Flags_Out(processor_1_flags_out), .INTin(INTs));
  // Probe on register_1_q
  Register #(.width(32)) register_1 (.Q(register_1_q));  // open: D, en, clk, clr
  LED led_2 (.in(debug_control_panel_1_break_enabled));
  // Probe on debug_control_panel_1_r0_data
  // Probe on debug_control_panel_1_r1_data
  // Probe on debug_control_panel_1_r2_data
  // Probe on debug_control_panel_1_r3_data
  // Probe on debug_control_panel_1_r4_data
  // Probe on debug_control_panel_1_r5_data
  // Probe on debug_control_panel_1_r6_data
  // Probe on debug_control_panel_1_r7_data
  Button button_1 (.out(button_1_out));
  Button button_2 (.out(button_2_out));
  Main_Memory main_memory_1 (
    .CLK(Clk), .in_2(Clr), .in_3(Write), .in_4(Read), .Address_Bus(Addrs),
    .Data_Bus_In(processor_1_processor_data_bus_out), .Data_Bus_Out(main_memory_1_data_bus_out));
  LED led_3 (.in(debug_control_panel_1_tick_sensor));
  // Probe on debug_control_panel_1_r8_data
  // Probe on debug_control_panel_1_r9_data
  // Probe on debug_control_panel_1_r10_data
  // Probe on debug_control_panel_1_r11_data
  // Probe on debug_control_panel_1_r12_data
  // Probe on debug_control_panel_1_r13_data
  // Probe on debug_control_panel_1_r14_data
  // Probe on debug_control_panel_1_r15_data
  Button button_3 (.out(button_3_out));
  LED led_4 (.in(debug_control_panel_1_c));
  LED led_5 (.in(debug_control_panel_1_i));
  // Probe on I_Addrs
  // Probe on IR
  Button button_4 (.out(button_4_out));
  // Probe on debug_control_panel_1_instruction_counter
  LED led_6 (.in(debug_control_panel_1_v));
  LED led_7 (.in(debug_control_panel_1_n));
  LED led_8 (.in(debug_control_panel_1_z));
  Button button_5 (.out(button_5_out));
  I_O i_o_1 (
    .in_2(Clr), .in_3(Write), .in_4(Read), .Address_Bus(Addrs),
    .Data_Bus_In(processor_1_processor_data_bus_out), .CLK(Clk), .LEDout(LED),
    .Data_Bus_Out(main_memory_1_data_bus_out), .SWin(SW), .Hex0(H0), .Hex1(H1), .Trunning(i_o_1_trunning),
    .TReload(i_o_1_treload), .TCount(i_o_1_tcount), .Troll(i_o_1_troll), .INTout(INTs));
  Debug_Control_Panel debug_control_panel_1 (
    .Clock_Signal(Clk), .CState(State), .Step_input(button_4_out), .Run_input(button_3_out),
    .Go_1_Cycle_input(1'b0), .Clear_input(button_5_out), .Instr_Addrs(I_Addrs),
    .Interconnect_Address_Bus(Addrs), .Running(debug_control_panel_1_running),
    .Reg_Wirte(processor_1_debug_reg_write), .Reg_Addr(processor_1_debug_reg_addrs),
    .Reg_Data_In(processor_1_debug_data_out), .R15_Data(debug_control_panel_1_r15_data),
    .R14_Data(debug_control_panel_1_r14_data), .R13_Data(debug_control_panel_1_r13_data),
    .R0_Data(debug_control_panel_1_r0_data), .R1_Data(debug_control_panel_1_r1_data),
    .R2_Data(debug_control_panel_1_r2_data), .R3_Data(debug_control_panel_1_r3_data),
    .R4_Data(debug_control_panel_1_r4_data), .R5_Data(debug_control_panel_1_r5_data),
    .R6_Data(debug_control_panel_1_r6_data), .R7_Data(debug_control_panel_1_r7_data),
    .R12_Data(debug_control_panel_1_r12_data), .R11_Data(debug_control_panel_1_r11_data),
    .R10_Data(debug_control_panel_1_r10_data), .R9_Data(debug_control_panel_1_r9_data),
    .R8_Data(debug_control_panel_1_r8_data), .Flags_In(processor_1_flags_out), .C(debug_control_panel_1_c),
    .Z(debug_control_panel_1_z), .N(debug_control_panel_1_n), .V(debug_control_panel_1_v),
    .Tick_Sensor(debug_control_panel_1_tick_sensor), .STOP__input(button_2_out), .Break_Addr(register_1_q),
    .Break_En_Dis(button_1_out), .Break_Enabled(debug_control_panel_1_break_enabled), .Clr_out(Clr),
    .Instruction_Counter(debug_control_panel_1_instruction_counter), .I(debug_control_panel_1_i));  // open: out_15, out_19, out_16
  Hex_Digit_Display hex_digit_display_1 (.value(H1));  // open: dp
  // Probe on i_o_1_treload
  // Probe on i_o_1_tcount
  LED led_9 (.in(LED));
  T_Flip_Flop t_ff_1 (.T(1'b1), .Q(SW), .reset(Clr));  // open: clk, Qn, preset, en
  Hex_Digit_Display hex_digit_display_2 (.value(H0));  // open: dp
  LED led_10 (.in(i_o_1_troll));
  LED led_11 (.in(i_o_1_trunning));

  // Notes on the sheet:
  //   Clock signal to system
  //   Debug
  //   Signals
  //   Debugger Version 4 - 5
  //   Interconnect Data Bus in 2 directions = artefact of Logisim :(
  //   Interconnect Address Bus
  //   Switch
  //   External Devices
  //   Timer Running
  //   Addrs: 0x8000 0100
  //   Addrs: 0x8000 0200
  //   Timer Rolled
  //   Timer Reload Value
  //   Timer Current Value
  //   Control Addrs: 0x8000 0300
  //   Data Addrs:     0x8000 0301
endmodule

module Processor (
  input  CLK,
  input  Clr,
  input  [31:0] Processor_Data_In,
  input  [7:0] INTin,
  output [31:0] IReg,
  output Debug_Reg_Write,
  output [3:0] Debug_Reg_Addrs,
  output [31:0] Debug_Data_out,
  output [6:0] CurrState,
  output [31:0] Address_Bus,
  output [31:0] Processor_Data_Bus_Out,
  output MWrite,
  output MRead,
  output [4:0] Flags_Out
);

  wire _20_16, AADD, ALUF, and_1_out, and_3_out, and_4_out, and_5_out, and_6_out, and_9_out, C1OE, ccNoGo,
       Cflag, ClearIF, CN1OE, cTest, cTrue, IActive, iClk, IF, Iflag, imm, IRCE, iTest, iTimer, LROE, MARCE,
       MAROE, MDRCE, MDRget, MDROE, MDRput, moreRegs, Nflag, not_2_out, not_3_out, not_4_out, not_5_out,
       not_6_out, not_7_out, or_1_out, or_2_out, or_3_out, or_4_out, or_5_out, or_6_out, pChoice, PCOE,
       pLatch, pNoGo, pReg, pShift, PSROE, pTest, R0OE, R1OE, R2OE, R3OE, S_U, SetIF, SPOE, State_High_Bit,
       VAddrs, Vflag, xor_1_out, Zflag;
  wire [2:0] bitfinder_1_index;
  wire [3:0] bitfinder_2_index, bitfinder_3_index, controlled_buffer_7_out, Opr, pRid;
  wire [3:3] multiplexer_4_out;
  wire [4:0] rom_2_data_3;
  wire [5:0] rom_2_data;
  wire [6:0] multiplexer_1_out, multiplexer_2_out, multiplexer_3_out, rom_1_data;
  wire [10:6] rom_2_data_2;
  wire [11:11] multiplexer_5_out;
  wire [15:0] and_8_out, demultiplexer_1_out0, mask_reg_q, multiplexer_7_out, not_8_out;
  wire [19:19] rom_3_data;
  wire [31:0] adder_1_out, alu_1_r, controlled_buffer_14_out, controlled_buffer_18_out, MAR_debug_q,
       MDR_debug_q, MDR_dout, T1_debug_q, T1_dout, T2_debug_q;
  wire [31:5] controlled_buffer_6_out;

  and and_1 (and_1_out, CurrState[0], CurrState[1], ~CurrState[2], ~CurrState[3], ~CurrState[4], ~CurrState[5], ~CurrState[6]);  // AND_Gate
  not not_1 (iClk, CLK);
  ROM #(.dataWidth(7)) rom_1 (.addr(IReg[31:24]), .data(rom_1_data), .sel(and_1_out));
  Multiplexer #(.width(7)) multiplexer_1 (
    .in0({State_High_Bit, rom_2_data}), .in1(rom_1_data), .out(multiplexer_1_out), .sel(and_1_out));  // open: en
  or or_1 (or_1_out, ccNoGo, pNoGo);
  and and_2 (iTest, ~CurrState[0], ~CurrState[1], ~CurrState[2], ~CurrState[3], ~CurrState[4], ~CurrState[5], ~CurrState[6]);  // AND_Gate
  assign Opr = AADD ? 4'b0001 : 4'bz;  // Controlled_Buffer controlled_buffer_1
  Multiplexer #(.width(7)) multiplexer_2 (
    .in0(multiplexer_1_out), .in1({7{1'b0}}), .out(multiplexer_2_out), .sel(or_1_out));  // open: en
  Multiplexer #(.width(7)) multiplexer_3 (
    .in0(multiplexer_2_out), .in1(7'b1000000), .out(multiplexer_3_out), .sel(and_3_out));  // open: en
  and and_3 (and_3_out, IActive, Flags_Out[4], iTest);
  assign Opr = rom_2_data_3[4] ? IReg[27:24] : 4'bz;  // Controlled_Buffer controlled_buffer_2
  assign Opr = rom_2_data_3[3] ? 4'b0000 : 4'bz;  // Controlled_Buffer controlled_buffer_3
  Register #(.width(7)) State_Register (.D(multiplexer_3_out), .Q(CurrState), .clk(CLK), .clr(Clr));  // open: en
  // Probe on multiplexer_3_out
  Register #(.width(4)) PSR (.D({Cflag, Zflag, Nflag, Vflag}), .en(ALUF), .Q(Flags_Out[3:0]), .clk(iClk), .clr(Clr));
  D_Flip_Flop u_IF (.clk(iClk), .D(Iflag), .Q(Flags_Out[4]), .preset(SetIF), .en(IF), .reset(or_2_out));  // open: Qn
  or or_2 (or_2_out, ClearIF, Clr);
  // Probe on IReg
  Register #(.width(32)) Instruction_Register (.D(Debug_Data_out), .en(IRCE), .Q(IReg), .clk(iClk), .clr(Clr));
  assign Debug_Reg_Addrs = rom_2_data_3[2] ? IReg[23:20] : 4'bz;  // Controlled_Buffer D
  ROM #(.addrWidth(7), .dataWidth(29)) rom_2 (
    .addr(CurrState),
    .data({IRCE, PCOE, C1OE, AADD, MARCE, MAROE, MDRCE, MDROE, MDRput, MDRget, MRead, MWrite, rom_2_data_3, Debug_Reg_Write, rom_2_data_2, rom_2_data}));  // open: sel
  ROM #(.addrWidth(7), .dataWidth(24)) rom_3 (
    .addr(CurrState),
    .data({R3OE, R2OE, R1OE, R0OE, rom_3_data[19], VAddrs, IF, PSROE, SetIF, ClearIF, State_High_Bit, LROE, SPOE, pTest, CN1OE, pReg, pLatch, pShift, pChoice, cTest, ALUF, imm, _20_16, S_U}));  // open: sel
  assign Debug_Reg_Addrs = rom_2_data_3[1] ? IReg[19:16] : 4'bz;  // Controlled_Buffer SX
  assign Debug_Reg_Addrs = rom_2_data_3[0] ? IReg[15:12] : 4'bz;  // Controlled_Buffer SY
  T_Flip_Flop t_ff_1 (.Q(iTimer));  // open: clk, T, Qn, preset, reset, en
  not not_2 (not_2_out, Flags_Out[2]);
  not not_3 (not_3_out, Flags_Out[3]);
  not not_4 (not_4_out, Flags_Out[1]);
  not not_5 (not_5_out, Flags_Out[0]);
  xor xor_1 (xor_1_out, Flags_Out[0], Flags_Out[1]);
  and and_4 (and_4_out, not_2_out, Flags_Out[3]);
  not not_6 (not_6_out, xor_1_out);
  assign Debug_Data_out = PSROE ? {{27{1'b0}}, Flags_Out} : 32'bz;  // Controlled_Buffer controlled_buffer_4
  assign Debug_Reg_Addrs = PCOE ? 4'b1111 : 4'bz;  // Controlled_Buffer controlled_buffer_5
  // Probe on Debug_Reg_Addrs
  or or_3 (or_3_out, Debug_Reg_Write, rom_2_data_2[10]);
  // Probe on T1_debug_q
  // Probe on Debug_Data_out
  or or_4 (or_4_out, not_3_out, Flags_Out[2]);
  assign {controlled_buffer_6_out, Iflag, Vflag, Nflag, Zflag, Cflag} = and_5_out ? Debug_Data_out : 32'bz;  // Controlled_Buffer controlled_buffer_6
  Reg32 T1 (
    .DIn(Debug_Data_out), .CE(rom_2_data_2[9]), .DOut(T1_dout), .Debug_Q(T1_debug_q), .CLK(CLK),
    .OE(rom_2_data_2[8]));  // open: Clear
  // Probe on Opr
  BitFinder bitfinder_1 (.in(INTin), .index(bitfinder_1_index), .found(IActive));
  and and_5 (and_5_out, ALUF, IF);
  assign controlled_buffer_7_out = _20_16 ? IReg[19:16] : 4'bz;  // Controlled_Buffer controlled_buffer_7
  assign controlled_buffer_7_out = not_7_out ? {4{multiplexer_4_out[3]}} : 4'bz;  // Controlled_Buffer controlled_buffer_8
  not not_7 (not_7_out, _20_16);
  Multiplexer multiplexer_4 (.in0(1'b0), .in1(IReg[15]), .out(multiplexer_4_out[3]), .sel(S_U));  // open: en
  Multiplexer #(.select(2)) multiplexer_5 (
    .in0(1'b0), .in1(IReg[15]), .in2(1'b0), .in3(IReg[19]), .out(multiplexer_5_out[11]), .sel({_20_16, S_U}));  // open: en
  RAM #(.addrWidth(4), .dataWidth(32)) ram_1 (
    .addr(Debug_Reg_Addrs), .data(Debug_Data_out), .sel(or_3_out), .clk(iClk), .ld(rom_2_data_2[10]),
    .clr(Clr));
  // Probe on T1_dout
  // Probe on adder_1_out
  Adder #(.width(32)) adder_1 (.a({{29{1'b0}}, bitfinder_1_index}), .b(32'h1), .out(adder_1_out));  // open: cin, cout
  and and_6 (and_6_out, not_2_out, not_6_out);
  or or_5 (or_5_out, Flags_Out[2], xor_1_out);
  // Probe on alu_1_r
  ALU alu_1 (
    .X(T1_dout), .Y(Debug_Data_out), .Clock(CLK), .Opr(Opr), .R(alu_1_r), .C(Cflag), .V(Vflag), .S(Nflag),
    .Z(Zflag), .F(ALUF), .Clr_In(Clr));
  assign Debug_Data_out = VAddrs ? adder_1_out : 32'bz;  // Controlled_Buffer controlled_buffer_9
  assign Debug_Data_out = imm ? {{12{multiplexer_5_out[11]}}, controlled_buffer_7_out, IReg[15:0]} : 32'bz;  // Controlled_Buffer controlled_buffer_10
  // Probe on Debug_Data_out
  // Probe on Debug_Data_out
  // Probe on Debug_Data_out
  LED led_1 (.in(Cflag));
  LED led_2 (.in(Vflag));
  LED led_3 (.in(Nflag));
  LED led_4 (.in(Zflag));
  assign Debug_Data_out = C1OE ? 32'h1 : 32'bz;  // Controlled_Buffer controlled_buffer_11
  // Probe on T2_debug_q
  Reg32 T2 (
    .DIn(alu_1_r), .CE(rom_2_data_2[7]), .DOut(Debug_Data_out), .Debug_Q(T2_debug_q), .CLK(CLK),
    .OE(rom_2_data_2[6]));  // open: Clear
  Multiplexer #(.select(4)) multiplexer_6 (
    .in0(1'b0), .in1(Flags_Out[2]), .in2(not_2_out), .in3(Flags_Out[3]), .in4(not_3_out), .in5(Flags_Out[1]),
    .in6(not_4_out), .in7(Flags_Out[0]), .in8(not_5_out), .in9(and_4_out), .in10(or_4_out), .in11(not_6_out),
    .in12(xor_1_out), .in13(and_6_out), .in14(or_5_out), .in15(1'b1), .out(cTrue), .sel(IReg[23:20]));  // open: en
  Demultiplexer #(.select(4)) demultiplexer_1 (
    .out0(demultiplexer_1_out0[0]), .out1(demultiplexer_1_out0[1]), .out2(demultiplexer_1_out0[2]),
    .out3(demultiplexer_1_out0[3]), .out4(demultiplexer_1_out0[4]), .out5(demultiplexer_1_out0[5]),
    .out6(demultiplexer_1_out0[6]), .out7(demultiplexer_1_out0[7]), .out8(demultiplexer_1_out0[8]),
    .out9(demultiplexer_1_out0[9]), .out10(demultiplexer_1_out0[10]), .out11(demultiplexer_1_out0[11]),
    .out12(demultiplexer_1_out0[12]), .out13(demultiplexer_1_out0[13]), .out14(demultiplexer_1_out0[14]),
    .out15(demultiplexer_1_out0[15]), .in(1'b1), .sel(pRid));  // open: en
  assign Debug_Reg_Addrs = pReg ? pRid : 4'bz;  // Controlled_Buffer controlled_buffer_12
  assign Debug_Data_out = CN1OE ? {32{1'b1}} : 32'bz;  // Controlled_Buffer controlled_buffer_13
  // Probe on MDR_debug_q
  assign controlled_buffer_14_out = MDRput ? Debug_Data_out : 32'bz;  // Controlled_Buffer controlled_buffer_14
  assign controlled_buffer_14_out = MRead ? controlled_buffer_18_out : 32'bz;  // Controlled_Buffer controlled_buffer_15
  and and_7 (ccNoGo, ~cTrue, cTest);  // AND_Gate
  assign Debug_Reg_Addrs = PCOE ? 4'b1111 : 4'bz;  // Controlled_Buffer controlled_buffer_16
  assign Debug_Data_out = MDRget ? MDR_dout : 32'bz;  // Controlled_Buffer controlled_buffer_17
  Reg32 MDR (
    .DIn(controlled_buffer_14_out), .CE(MDRCE), .DOut(MDR_dout), .Debug_Q(MDR_debug_q), .CLK(CLK), .OE(MDROE));  // open: Clear
  // Probe on MDR_dout
  assign controlled_buffer_18_out = MWrite ? MDR_dout : 32'bz;  // Controlled_Buffer controlled_buffer_18
  assign not_8_out = ~demultiplexer_1_out0;  // NOT_Gate not_8, 16 bits wide
  assign and_8_out = mask_reg_q & not_8_out;  // AND_Gate and_8, 16 bits wide
  assign Debug_Reg_Addrs = LROE ? 4'b1110 : 4'bz;  // Controlled_Buffer controlled_buffer_19
  assign Debug_Reg_Addrs = SPOE ? 4'b1101 : 4'bz;  // Controlled_Buffer controlled_buffer_20
  // Probe on MAR_debug_q
  Reg32 MAR (
    .DIn(Debug_Data_out), .CE(MARCE), .DOut(Address_Bus), .Debug_Q(MAR_debug_q), .CLK(CLK), .OE(MAROE),
    .Clear(Clr));
  // Probe on multiplexer_7_out
  Multiplexer #(.width(16)) multiplexer_7 (
    .in0(IReg[15:0]), .in1(and_8_out), .out(multiplexer_7_out), .sel(moreRegs));  // open: en
  assign controlled_buffer_18_out = MRead ? Processor_Data_In : 32'bz;  // Controlled_Buffer controlled_buffer_21
  Register #(.width(16)) mask_reg (.D(multiplexer_7_out), .Q(mask_reg_q), .clk(or_6_out), .clr(Clr));  // open: en
  or or_6 (or_6_out, and_9_out, pLatch);
  and and_9 (and_9_out, pShift, moreRegs);
  assign Debug_Reg_Addrs = R0OE ? 4'b0000 : 4'bz;  // Controlled_Buffer controlled_buffer_22
  assign Debug_Reg_Addrs = R1OE ? 4'b0001 : 4'bz;  // Controlled_Buffer controlled_buffer_23
  assign Processor_Data_Bus_Out = MWrite ? controlled_buffer_18_out : 32'bz;  // Controlled_Buffer controlled_buffer_24
  BitFinder #(.width(16)) bitfinder_2 (.in(mask_reg_q), .index(bitfinder_2_index));  // open: found
  BitFinder #(.width(16), .\type ("high1")) bitfinder_3 (.in(mask_reg_q), .index(bitfinder_3_index), .found(moreRegs));
  and and_10 (pNoGo, ~moreRegs, pTest);  // AND_Gate
  Multiplexer #(.width(4)) multiplexer_8 (
    .in0(bitfinder_2_index), .in1(bitfinder_3_index), .out(pRid), .sel(pChoice));  // open: en
  // Probe on pRid
  assign Debug_Reg_Addrs = R2OE ? 4'b0010 : 4'bz;  // Controlled_Buffer controlled_buffer_25
  assign Debug_Reg_Addrs = R3OE ? 4'b0011 : 4'bz;  // Controlled_Buffer controlled_buffer_26

  // Other names for the same wires on the sheet: RegW = Debug_Reg_Write; MMWrite = MWrite; MMRead = MRead;
  //   PSRV = Flags_Out[0]; PSRN = Flags_Out[1]; PSRZ = Flags_Out[2]; PSRC = Flags_Out[3]; curI = Flags_Out[4];
  //   IR[31:0] = IReg; pMask[15:0] = IReg[15:0]; Clear = Clr; Current_State[6:0] = CurrState;
  //   Internal_Data_Bus[31:0] = Debug_Data_out; cc[3:0] = IReg[23:20]; RegAddrBus[3:0] = Debug_Reg_Addrs

  // Notes on the sheet:
  //   Decode State Detecter
  //   signals for PUSH/POP circuit
  //   Opcode field of IR
  //   contents of rom_1 (hex, n*v repeats v):
  //   28 4 4 29 4 4 4 29 4 4 4*0 4 4 17*0 7 7 a 7 7 7 10 7 7 4*0 7 7 1a b 1b 1d 11 14 17 19 32 37 0 0 2a
  //   2c 2f 31 5b 5a 5c 4*0 1e 9*0 24 5*0 23 40*0 26 0 0 3c 123*0 3f
  //   ALU ADD opcode
  //   Invert for latching as needed
  //   Decode State ROM
  //   cc MUX
  //   1st Execution State Detecter
  //   17
  //   16
  //   15
  //   14
  //   13
  //   12
  //   to ALU
  //   Control FSM
  //   i MUX
  //   11
  //   10
  //   9
  //   8
  //   7
  //   6
  //   5
  //   AOP
  //   ALU NOP opcode
  //   ANOP
  //   next state from ROM word
  //   signals for immediate data 
  //   onto Internal Data Bus
  //   Program Status Register
  //   Interrupt Flag
  //   to cTrue circuit
  //   Control FSM Outputs LO
  //   Control FSM Outputs HI
  //   DR
  //   SXR
  //   SYR
  //   contents of rom_2 (hex, n*v repeats v):
  //   9008601 6c40182 10288003 8008a40 a605 11586 c840 a608 10189 c840 c800 a60c 200018d 111804e cc800f
  //   28c800 10089 100a412 50c413 a20000 a615 2000196 1008052 a618 2001596 2000196 100a40e a61c 200158d
  //   200018d 1249f 8260 60001a1 8262 2004500 1009f c625 10100 20001a7 8008840 10000 12586 50a42b 28c800
  //   a62d 20001ae c840 a630 20015ae 20001ae 8633 20001b4 1008a75 508436 a28033 1008638 60001b9 c4803a
  //   28883b 1008a78 80104bd 8866 0 3f 8601 2000182 1008243 508004 2a20185 1008246 8508407 2a20188 1008249
  //   50840a 2a2018b 100824c 50840d 2a2018e 100824f 508410 2a20191 1008252 508413 2a20194 1008855 508416
  //   a28017 1008018 c48019 8288800 8000 8000 100861d 6c4019e 28881f 1008260 6c401a1 288822 1008263
  //   6c401a4 288825 1008266 6c401a7 288828 1008269 6c401aa 28882b 100826c 6c401ad 828882e 100826f 6c401b0
  //   8288031 8840
  //   contents of rom_3 (hex, n*v repeats v):
  //   5*0 8 0 0 c 0 6 0 5 0 0 0 6 4*0 5 0 0 0 7 0 0 0 7 4*0 8 6 0 e 17 0 0 80 0 0 0 5 0 0 0 5 880 600 800
  //   120 60 880 400 0 100 840 10 1000 0 0 2800 2200 2000 12000 2200 2000 2000 2200 2000 3000 2200 2000
  //   802000 2200 2000 402000 2200 2000 202000 2200 2800 102000 2000 46000 2000 0 8000 4000 2800 2000
  //   102000 2000 2000 202000 2000 2000 402000 2000 2000 802000 2000 2000 3000 5*2000 22008 800
  //   signals for instruction fetch
  //   For now ... iTimer == 0
  //   (C==1) && (Z==0)
  //   N != V
  //   Immediate Operand Circuit
  //   Reg Address Bus
  //   RegR
  //   (C==0) || (Z==1)
  //   bit 15
  //   bit 19
  //   PC Reg Address
  //   cTrue Circuit to test Condition Code
  //   N == V
  //   16 x 32-bit Registers
  //   Interrupt Vector Address Generator
  //   ((Z==0) && (N==V)
  //   (Z==1) || (N!=V)
  //   Constant 1
  //   not in table
  //   always
  //   Interconnect Data Bus
  //   Interconnect Address Bus
  //   Constant -1
  //   MUX: picks the 1 to eliminate
  //   PC Reg Address
  //   Input:   pMask: imm16 from IR
  //   Input:   Clear: from Debug circuit
  //   AND: eliminates a 1
  //   from mask
  //   LR Reg Address
  //   SP Reg Address
  //   Circuit to handle mask shifting and register identification during PUSH/POP
  //   Inputs from Contol FSM outputs:
  //   pLatch: to latch the mask into the shift reg
  //   pShift: to clock the shift reg
  //   pChoice: to pick PUSH (1) vs POP (0)
  //   pReg: to drive reg id onto RegAddrsBus
  //   R0 Reg Address
  //   R0 Reg Address
  //   0:   lo to hi
  //   1:   hi to lo
  //   signal to ccMUX
  //   R0 Reg Address
  //   R0 Reg Address
endmodule

module Main_Memory (
  input  CLK,
  input  in_2,
  input  in_3,
  input  in_4,
  input  [31:0] Address_Bus,
  input  [31:0] Data_Bus_In,
  output [31:0] Data_Bus_Out
);

  wire and_1_out, button_1_out, comparator_1_eq, iClk, or_1_out;
  wire [31:0] ram_1_data;

  not not_1 (iClk, CLK);
  // Probe on Address_Bus
  // Probe on Address_Bus[10:0]
  and and_1 (and_1_out, comparator_1_eq, or_1_out);
  Comparator #(.width(21), .mode("unsigned")) comparator_1 (
    .a(Address_Bus[31:11]), .b({21{1'b0}}), .eq(comparator_1_eq));  // open: gt, lt
  // Probe on ram_1_data
  Button button_1 (.out(button_1_out));
  or or_1 (or_1_out, in_3, in_4);
  RAM #(.addrWidth(11), .dataWidth(32)) ram_1 (
    .addr(Address_Bus[10:0]), .data(ram_1_data), .sel(and_1_out), .clk(iClk), .ld(in_4), .clr(button_1_out));
  assign ram_1_data = in_3 ? Data_Bus_In : 32'bz;  // Controlled_Buffer controlled_buffer_1
  assign Data_Bus_Out = in_4 ? ram_1_data : 32'bz;  // Controlled_Buffer controlled_buffer_2

  // Other names for the same wires on the sheet: Clear = in_2; MMRead = in_4; MMWrite = in_3

  // Notes on the sheet:
  //   2 K  x 32-bit Memory
  //   RAM Address Range:
  //   0000 0000 to 0000 0400
endmodule

module I_O (
  input  SWin,
  input  in_2,
  input  in_3,
  input  in_4,
  input  [31:0] Address_Bus,
  input  [31:0] Data_Bus_In,
  input  CLK,
  output Trunning,
  output [3:0] Hex0,
  output [3:0] Hex1,
  output [31:0] TReload,
  output [31:0] TCount,
  output LEDout,
  output Troll,
  output [7:0] INTout,
  output [31:0] Data_Bus_Out
);

  wire _0___Count, and_1_out, and_2_out, and_3_out, and_4_out, and_5_out, and_6_out, and_7_out, and_9_out,
       and_10_out, and_14_out, and_17_out, comparator_1_eq, comparator_2_eq, comparator_3_eq,
       comparator_4_eq, comparator_5_eq, comparator_6_eq, comparator_7_eq, comparator_8_eq, comparator_9_eq,
       comparator_10_eq, comparator_11_eq, Do_Clear_Rollover, Do_Timer_Reset, Hex0On, Hex1On, iClk, or_1_out,
       or_2_out, register_1_q, Resetting_Timer, Roll_Clear, T_Clear, T_Control, TC_Write, TClk,
       Timer_Rollover, Timer_UNUSED, TimerIntEnable;
  wire [1:0] counter_2_q;
  wire [7:0] Hex_Data_Register_q;
  wire [31:0] Data;
  wire [31:2] Timer_Control_Register_q;

  Comparator #(.width(32), .mode("unsigned")) comparator_1 (
    .a(Address_Bus), .b(32'h80000301), .eq(comparator_1_eq));  // open: gt, lt
  and and_1 (and_1_out, comparator_2_eq, in_3);
  Comparator #(.width(32), .mode("unsigned")) comparator_2 (
    .a(Address_Bus), .b(32'h80000100), .eq(comparator_2_eq));  // open: gt, lt
  Register Hex_Data_Register (.D(Data[7:0]), .en(and_2_out), .Q(Hex_Data_Register_q), .clk(iClk), .clr(in_2));
  and and_2 (and_2_out, comparator_1_eq, in_3);
  Register #(.width(1)) LED_Register (.D(Data[0]), .en(and_1_out), .Q(LEDout), .clk(iClk), .clr(in_2));
  assign Data = in_3 ? Data_Bus_In : 32'bz;  // Controlled_Buffer controlled_buffer_1
  assign Data_Bus_Out = in_4 ? Data : 32'bz;  // Controlled_Buffer controlled_buffer_2
  assign Hex0 = Hex0On ? Hex_Data_Register_q[3:0] : 4'bz;  // Controlled_Buffer controlled_buffer_3
  assign Hex1 = Hex1On ? Hex_Data_Register_q[7:4] : 4'bz;  // Controlled_Buffer controlled_buffer_4
  Comparator #(.width(32), .mode("unsigned")) comparator_3 (
    .a(Address_Bus), .b(32'h80000201), .eq(comparator_3_eq));  // open: gt, lt
  and and_3 (and_3_out, comparator_3_eq, in_3);
  assign Data = and_4_out ? {{31{1'b0}}, SWin} : 32'bz;  // Controlled_Buffer controlled_buffer_5
  and and_4 (and_4_out, comparator_4_eq, in_4);
  Comparator #(.width(32), .mode("unsigned")) comparator_4 (
    .a(Address_Bus), .b(32'h80000200), .eq(comparator_4_eq));  // open: gt, lt
  Register #(.width(1)) register_1 (.D(Data[0]), .en(and_3_out), .Q(register_1_q), .clk(iClk), .clr(in_2));
  Comparator #(.width(32), .mode("unsigned")) comparator_5 (
    .a(Address_Bus), .b(32'h80000202), .eq(comparator_5_eq));  // open: gt, lt
  not not_1 (iClk, CLK);
  and and_5 (and_5_out, comparator_6_eq, in_3);
  Comparator #(.width(32), .mode("unsigned")) comparator_6 (
    .a(Address_Bus), .b(32'h80000300), .eq(comparator_6_eq));  // open: gt, lt
  D_Flip_Flop d_ff_1 (.clk(SWin), .D(1'b1), .Q(INTout[6]), .en(register_1_q), .reset(or_1_out));  // open: Qn, preset
  or or_1 (or_1_out, and_6_out, in_2);
  and and_6 (and_6_out, comparator_5_eq, in_3);
  Register #(.width(2)) Hex_Control_Register (
    .D(Data[1:0]), .en(and_5_out), .Q({Hex1On, Hex0On}), .clk(iClk), .clr(in_2));
  Comparator #(.width(32), .mode("unsigned")) comparator_7 (
    .a(Address_Bus), .b(32'h80000401), .eq(comparator_7_eq));  // open: gt, lt
  Register #(.width(32)) LED_Register_2 (.D(Data), .en(and_7_out), .Q(TReload), .clk(iClk), .clr(in_2));
  and and_7 (and_7_out, comparator_7_eq, in_3);
  Comparator #(.width(32), .mode("unsigned")) comparator_8 (
    .a(Address_Bus), .b(32'h80000400), .eq(comparator_8_eq));  // open: gt, lt
  D_Flip_Flop d_ff_2 (.clk(TClk), .D(1'b1), .Q(Troll), .en(Timer_Rollover), .reset(Roll_Clear));  // open: Qn, preset
  Register #(.width(32)) Timer_Control_Register (
    .D(Data), .en(TC_Write),
    .Q({Timer_Control_Register_q[31:5], TimerIntEnable, Timer_Control_Register_q[3:2], Timer_UNUSED, Trunning}),
    .clk(iClk), .clr(in_2));
  and and_8 (TC_Write, comparator_8_eq, in_3);
  assign Data = and_9_out ? {{31{1'b0}}, Troll} : 32'bz;  // Controlled_Buffer controlled_buffer_6
  and and_9 (and_9_out, comparator_9_eq, in_4);
  Comparator #(.width(32), .mode("unsigned")) comparator_9 (
    .a(Address_Bus), .b(32'h80000402), .eq(comparator_9_eq));  // open: gt, lt
  assign Data = and_10_out ? TCount : 32'bz;  // Controlled_Buffer controlled_buffer_7
  and and_10 (and_10_out, comparator_10_eq, in_4);
  Comparator #(.width(32), .mode("unsigned")) comparator_10 (
    .a(Address_Bus), .b(32'h80000403), .eq(comparator_10_eq));  // open: gt, lt
  or or_2 (or_2_out, Timer_Rollover, Resetting_Timer);
  Counter #(.width(32), .max('hffffffff)) counter_1 (
    .load(1'b1), .D(TReload), .count(T_Control), .Q(TCount), .clk(TClk), .clr(T_Clear));  // open: carry
  and and_11 (T_Control, ~or_2_out, Trunning);  // AND_Gate
  and and_12 (Do_Timer_Reset, TC_Write, Data[2]);
  and and_13 (INTout[2], TimerIntEnable, Troll);
  and and_14 (and_14_out, Trunning, CLK);
  Comparator #(.width(32), .mode("unsigned")) comparator_11 (
    .a(TCount), .b({32{1'b0}}), .gt(_0___Count), .eq(comparator_11_eq));  // open: lt
  or or_3 (T_Clear, in_2, Do_Timer_Reset);
  and and_15 (Do_Clear_Rollover, TC_Write, Data[3]);
  Counter #(.width(2), .max('h3)) counter_2 (
    .Q(counter_2_q), .clk(and_14_out), .clr(in_2));  // open: load, D, count, carry
  not not_2 (TClk, counter_2_q[1]);
  and and_16 (Timer_Rollover, comparator_11_eq, ~Resetting_Timer);  // AND_Gate
  D_Flip_Flop d_ff_3 (.Q(Resetting_Timer), .preset(Do_Timer_Reset), .en(1'b1), .reset(and_17_out));  // open: clk, D, Qn
  and and_17 (and_17_out, Resetting_Timer, _0___Count);
  or or_4 (Roll_Clear, Do_Clear_Rollover, in_2);

  assign {INTout[7], INTout[5:3], INTout[1:0]} = {6{1'b0}};

  // Other names for the same wires on the sheet: SWsignal = SWin; T_Roll = Troll; Timer_Start = Trunning;
  //   Addrs[31:0] = Address_Bus; Clear = in_2; Timer_Reset = Data[2]; Timer_Clear_Rollover = Data[3];
  //   TIMERint = INTout[2]; SWint = INTout[6]; MMRead = in_4; MMWrite = in_3; Timer_Reload[31:0] = TReload;
  //   Timer_Ticks[31:0] = TCount

  // Notes on the sheet:
  //   Hex Display Output:  Address = 0x80000301
  //   LED Output:  Address = 0x80000100
  //   Write 1 to 0x8000 0201 to enable switch interrupt
  //   Switch input:  Address = 0x80000200
  //   Switch Interrupt Latch
  //   Write any value to address 0x8000 0202 to clear switch interrupt
  //   Hex Display Control:  Address = 0x80000300
  //   Timer Control Output:  Address = 0x80000400
  //   Timer Reload Output:  Address = 0x80000401
  //   Timer Status Input:  Address = 0x80000402
  //   Timer Current Count Input:  Address = 0x80000403
  //   Count Down Timer
  //   These bits only have meaning while writing to the register
  //   These bits are latched and are persistent
  //   Timer Clock = System Clock / 4
endmodule

module Debug_Control_Panel (
  input  Step_input,
  input  Run_input,
  input  STOP__input,
  input  Clear_input,
  input  [6:0] CState,
  input  Go_1_Cycle_input,
  input  [31:0] Interconnect_Address_Bus,
  input  [31:0] Reg_Data_In,
  input  Reg_Wirte,
  input  [4:0] Flags_In,
  input  [3:0] Reg_Addr,
  input  Break_En_Dis,
  input  [31:0] Break_Addr,
  output Clr_out,
  output out_15,
  output out_16,
  output Clock_Signal,
  output Running,
  output out_19,
  output [31:0] Instr_Addrs,
  output [31:0] R8_Data,
  output [31:0] R0_Data,
  output [31:0] R9_Data,
  output [31:0] R1_Data,
  output [31:0] R10_Data,
  output [31:0] R2_Data,
  output V,
  output N,
  output Z,
  output [31:0] R11_Data,
  output [31:0] R3_Data,
  output C,
  output I,
  output [31:0] R12_Data,
  output [31:0] R4_Data,
  output [31:0] R13_Data,
  output [31:0] R5_Data,
  output [31:0] R14_Data,
  output [31:0] R6_Data,
  output Tick_Sensor,
  output [31:0] R15_Data,
  output [31:0] Instruction_Counter,
  output [31:0] R7_Data,
  output Break_Enabled
);

  wire _1_Cycle, _1_Cycle_Select_qn, _02cnt_q, and_1_out, and_3_out, and_5_out, and_9_out, and_10_out,
       and_11_out, and_12_out, and_13_out, and_14_out, and_15_out, and_16_out, and_18_out, and_19_out,
       and_20_out, and_21_out, and_22_out, and_23_out, and_24_out, and_25_out, BRK, comparator_1_eq,
       comparator_2_gt, comparator_3_eq, comparator_6_lt, Debug_stop, Fetched_Instruction, Fetching, iClk,
       internal_clock, not_1_out, not_2_out, not_3_out, not_4_out, not_5_out, not_6_out, not_7_out,
       not_8_out, not_9_out, not_10_out, not_11_out, not_12_out, not_13_out, not_14_out, not_15_out,
       not_16_out, not_17_out, not_19_out, not_20_out, not_21_out, not_22_out, not_23_out, not_24_out,
       not_25_out, not_26_out, not_27_out, not_28_out, not_29_out, or_1_out, or_2_out, or_3_out, or_4_out,
       or_5_out, or_6_out, or_7_out, or_8_out, or_9_out, or_10_out, R0, R1, R2, R3, R4, R5, R6, R7, R8, R9,
       R10, R11, R12, R13, R14, R15, Run_pulse, Run_Select_qn, State0, Step_pulse, Step_Select_qn,
       Stop_pulse, Stop_select, STOP_Select_qn, t_ff_1_qn, t_ff_2_q, t_ff_3_q, t_ff_4_q, t_ff_6_q;
  wire [31:0] curIAddrs;

  not not_1 (not_1_out, Step_input);
  or or_1 (or_1_out, State0, Step_pulse, Clr_out, Debug_stop);
  or or_2 (or_2_out, Debug_stop, BRK, Clr_out);
  T_Flip_Flop t_ff_1 (.clk(Clock_Signal), .T(t_ff_1_qn), .Qn(t_ff_1_qn), .reset(_1_Cycle));  // open: Q, preset, en
  not not_2 (not_2_out, not_4_out);
  not not_3 (not_3_out, not_1_out);
  not not_4 (not_4_out, not_3_out);
  Comparator #(.width(7), .mode("unsigned")) comparator_1 (
    .a(CState), .b(7'b0000010), .eq(comparator_1_eq));  // open: gt, lt
  Comparator #(.width(7), .mode("unsigned")) comparator_2 (
    .a(CState), .b(7'b0000011), .gt(comparator_2_gt));  // open: eq, lt
  T_Flip_Flop t_ff_2 (
    .clk(Fetched_Instruction), .T(1'b1), .Q(t_ff_2_q), .preset(or_3_out), .en(t_ff_2_q));  // open: Qn, reset
  or or_3 (or_3_out, Step_pulse, Clr_out);
  T_Flip_Flop t_ff_3 (.clk(Run_pulse), .T(1'b1), .Q(t_ff_3_q), .reset(or_2_out));  // open: Qn, preset, en
  T_Flip_Flop t_ff_4 (
    .clk(internal_clock), .T(1'b1), .Q(t_ff_4_q), .Qn(Tick_Sensor), .preset(t_ff_4_q), .reset(Clr_out));  // open: en
  Comparator #(.width(32), .mode("unsigned")) comparator_3 (
    .a(curIAddrs), .b(Break_Addr), .eq(comparator_3_eq));  // open: gt, lt
  not not_5 (not_5_out, not_2_out);
  not not_6 (not_6_out, _02cnt_q);
  Counter #(.width(1), .max('h1)) _02cnt (
    .count(not_6_out), .Q(_02cnt_q), .clk(comparator_1_eq), .clr(or_1_out));  // open: load, D, carry
  and and_1 (and_1_out, _02cnt_q, not_7_out);
  Comparator #(.width(7), .mode("unsigned")) comparator_4 (.a(CState), .b({7{1'b0}}), .eq(State0));  // open: gt, lt
  T_Flip_Flop t_ff_5 (.clk(Break_En_Dis), .T(1'b1), .Q(Break_Enabled), .reset(Clr_out));  // open: Qn, preset, en
  and and_2 (Step_pulse, Step_input, not_5_out);
  Counter #(.width(1), .max('h1)) _03cnt (
    .count(and_1_out), .Q(Fetched_Instruction), .clk(comparator_2_gt), .clr(or_1_out));  // open: load, D, carry
  not not_7 (not_7_out, Fetched_Instruction);
  or or_4 (or_4_out, t_ff_2_q, t_ff_3_q, 1'b0);
  and and_3 (and_3_out, Break_Enabled, comparator_3_eq, Fetched_Instruction);
  Comparator #(.width(7)) comparator_5 (.a(CState), .b(7'b0111111), .eq(BRK));  // open: gt, lt
  Demultiplexer #(.select(4)) demultiplexer_1 (
    .out0(R0), .out1(R1), .out2(R2), .out3(R3), .out4(R4), .out5(R5), .out6(R6), .out7(R7), .out8(R8),
    .out9(R9), .out10(R10), .out11(R11), .out12(R12), .out13(R13), .out14(R14), .out15(R15), .in(1'b1),
    .sel(Reg_Addr));  // open: en
  T_Flip_Flop t_ff_6 (.clk(Fetched_Instruction), .T(1'b1), .Q(t_ff_6_q), .reset(or_5_out));  // open: Qn, preset, en
  or or_5 (or_5_out, Clr_out, State0, and_5_out);
  or or_6 (or_6_out, and_3_out, Stop_select);
  not not_8 (not_8_out, Run_input);
  Clock clock_1 (.out(internal_clock));
  and and_4 (Running, ~BRK, or_4_out);  // AND_Gate
  and and_5 (and_5_out, t_ff_6_q, iClk);
  not not_9 (not_9_out, not_8_out);
  not not_10 (not_10_out, not_9_out);
  T_Flip_Flop Clock_Gate (.clk(internal_clock), .T(Running), .Q(Clock_Signal), .en(1'b1));  // open: Qn, preset, reset
  Counter #(.width(32), .max('hffffffff)) instr_count (
    .Q(Instruction_Counter), .clk(and_5_out), .clr(Clr_out));  // open: load, D, count, carry
  not not_11 (not_11_out, not_10_out);
  not not_12 (not_12_out, not_11_out);
  not not_13 (not_13_out, Go_1_Cycle_input);
  not not_14 (not_14_out, not_13_out);
  // Probe on CState
  Counter counter_1 (.clk(Fetched_Instruction), .clr(Clr_out));  // open: load, D, count, Q, carry
  and and_6 (Debug_stop, Fetched_Instruction, or_6_out);
  and and_7 (Run_pulse, Run_input, not_12_out);
  not not_15 (not_15_out, not_14_out);
  not not_16 (not_16_out, not_17_out);
  not not_17 (not_17_out, not_15_out);
  not not_18 (iClk, Clock_Signal);
  not not_19 (not_19_out, comparator_6_lt);
  assign Instr_Addrs = not_19_out ? curIAddrs : 32'bz;  // Controlled_Buffer controlled_buffer_1
  and and_8 (_1_Cycle, Go_1_Cycle_input, not_16_out);
  Reg32 reg32_1 (
    .DIn(Interconnect_Address_Bus), .CE(Fetching), .DOut(curIAddrs), .CLK(iClk), .OE(1'b1), .Clear(Clr_out));  // open: Debug_Q
  Comparator #(.width(7), .mode("unsigned")) comparator_6 (
    .a(CState), .b(7'b0000001), .eq(Fetching), .lt(comparator_6_lt));  // open: gt
  Register #(.width(32)) register_1 (.D(Reg_Data_In), .en(and_9_out), .Q(R0_Data), .clk(iClk), .clr(Clr_out));
  and and_9 (and_9_out, R0, Reg_Wirte);
  Register #(.width(32)) register_2 (.D(Reg_Data_In), .en(and_10_out), .Q(R1_Data), .clk(iClk), .clr(Clr_out));
  and and_10 (and_10_out, R1, Reg_Wirte);
  Register #(.width(32)) register_3 (.D(Reg_Data_In), .en(and_11_out), .Q(R2_Data), .clk(iClk), .clr(Clr_out));
  and and_11 (and_11_out, R2, Reg_Wirte);
  Register #(.width(32)) register_4 (.D(Reg_Data_In), .en(and_12_out), .Q(R3_Data), .clk(iClk), .clr(Clr_out));
  and and_12 (and_12_out, R3, Reg_Wirte);
  Register #(.width(32)) register_5 (.D(Reg_Data_In), .en(and_13_out), .Q(R4_Data), .clk(iClk), .clr(Clr_out));
  and and_13 (and_13_out, R4, Reg_Wirte);
  Register #(.width(32)) register_6 (.D(Reg_Data_In), .en(and_14_out), .Q(R5_Data), .clk(iClk), .clr(Clr_out));
  and and_14 (and_14_out, R5, Reg_Wirte);
  Register #(.width(32)) register_7 (.D(Reg_Data_In), .en(and_15_out), .Q(R6_Data), .clk(iClk), .clr(Clr_out));
  and and_15 (and_15_out, R6, Reg_Wirte);
  Register #(.width(32)) register_8 (.D(Reg_Data_In), .en(and_16_out), .Q(R7_Data), .clk(iClk), .clr(Clr_out));
  and and_16 (and_16_out, R7, Reg_Wirte);
  not not_20 (not_20_out, STOP__input);
  not not_21 (not_21_out, not_20_out);
  not not_22 (not_22_out, not_21_out);
  not not_23 (not_23_out, not_24_out);
  not not_24 (not_24_out, not_22_out);
  and and_17 (Stop_pulse, STOP__input, not_23_out);
  T_Flip_Flop Step_Select (
    .clk(Step_pulse), .T(1'b1), .Q(out_19), .Qn(Step_Select_qn), .reset(or_7_out), .en(Step_Select_qn));  // open: preset
  or or_7 (or_7_out, Stop_pulse, Clr_out, Run_pulse);
  T_Flip_Flop _1_Cycle_Select (
    .T(1'b1), .Q(out_15), .Qn(_1_Cycle_Select_qn), .reset(or_8_out), .en(_1_Cycle_Select_qn));  // open: clk, preset
  or or_8 (or_8_out, Step_pulse, Clr_out, Run_pulse);
  Register #(.width(32)) register_9 (.D(Reg_Data_In), .en(and_18_out), .Q(R8_Data), .clk(iClk), .clr(Clr_out));
  and and_18 (and_18_out, R8, Reg_Wirte);
  Register #(.width(32)) register_10 (.D(Reg_Data_In), .en(and_19_out), .Q(R9_Data), .clk(iClk), .clr(Clr_out));
  and and_19 (and_19_out, R9, Reg_Wirte);
  Register #(.width(32)) register_11 (.D(Reg_Data_In), .en(and_20_out), .Q(R10_Data), .clk(iClk), .clr(Clr_out));
  and and_20 (and_20_out, R10, Reg_Wirte);
  Register #(.width(32)) register_12 (.D(Reg_Data_In), .en(and_21_out), .Q(R11_Data), .clk(iClk), .clr(Clr_out));
  and and_21 (and_21_out, R11, Reg_Wirte);
  Register #(.width(32)) register_13 (.D(Reg_Data_In), .en(and_22_out), .Q(R12_Data), .clk(iClk), .clr(Clr_out));
  and and_22 (and_22_out, R12, Reg_Wirte);
  Register #(.width(32)) register_14 (.D(Reg_Data_In), .en(and_23_out), .Q(R13_Data), .clk(iClk), .clr(Clr_out));
  and and_23 (and_23_out, R13, Reg_Wirte);
  Register #(.width(32)) register_15 (.D(Reg_Data_In), .en(and_24_out), .Q(R14_Data), .clk(iClk), .clr(Clr_out));
  and and_24 (and_24_out, R14, Reg_Wirte);
  Register #(.width(32)) register_16 (.D(Reg_Data_In), .en(and_25_out), .Q(R15_Data), .clk(iClk), .clr(Clr_out));
  and and_25 (and_25_out, R15, Reg_Wirte);
  not not_25 (not_25_out, not_26_out);
  not not_26 (not_26_out, Clear_input);
  not not_27 (not_27_out, not_25_out);
  not not_28 (not_28_out, not_27_out);
  not not_29 (not_29_out, not_28_out);
  T_Flip_Flop Run_Select (
    .clk(Run_pulse), .T(1'b1), .Q(out_16), .Qn(Run_Select_qn), .reset(or_9_out), .en(Run_Select_qn));  // open: preset
  and and_26 (Clr_out, Clear_input, not_29_out);
  or or_9 (or_9_out, Step_pulse, Clr_out, Stop_pulse);
  T_Flip_Flop u_STOP_Select (
    .clk(Stop_pulse), .T(1'b1), .Q(Stop_select), .Qn(STOP_Select_qn), .reset(or_10_out), .en(STOP_Select_qn));  // open: preset
  or or_10 (or_10_out, Step_pulse, Clr_out, Run_pulse);

  assign C = Flags_In[3];
  assign I = Flags_In[4];
  assign N = Flags_In[1];
  assign V = Flags_In[0];
  assign Z = Flags_In[2];

  // Other names for the same wires on the sheet: _1_C_select = out_15; _1C = Go_1_Cycle_input;
  //   Addrs[31:0] = Interconnect_Address_Bus; Clk_Out = Clock_Signal; Clear_pulse = Clr_out; Clr = Clr_out;
  //   CurState[6:0] = CState; Reg_Data[31:0] = Reg_Data_In; RegWrite = Reg_Wirte; Run_select = out_16

  // Notes on the sheet:
  //   FLAG Output LEDs
  //   Are Ticks Enabled?
  //   disconnected 1 cycle control
  //   just entered first execution state
  //   detect start of new fetch stage
  //   Break Logic: STOP button or break address
  //   the inverters + AND on the input signal clips the input to create a short pulse so that the length of time the button is pressed doesn't matter
  //   Breakpoint instruction detecter
  //   Signals used to latch changes in register values
  //   latch current Instruction Address
  //   was used for stepping one cycle
  //   this input in not used
  //   disconnect 1 Cycle control
  //   Step button was pressed
  //   Register Values
  //   Run button was pressed
  //   Stop button was pressed
endmodule
